# Fritzing sketch USB тестер (saved by Fritzing 0.9.3b)

parts:
  OLED_I2C1 = OLED 128x64 I2C Monochrome Display
  R2 = Resistor [tolerance=±5% resistance=1k package=THT]
  R1 = Resistor [tolerance=±5% resistance=0.1 power=2W package=THT]
  X3 = USB Connectors [package=usb-a-h]
  X4 = USB Connectors [package=usb-a-h]
  R3 = Resistor [tolerance=±5% resistance=20k package=THT]
  R4 = Resistor [tolerance=±5% resistance=1k package=THT]
  R5 = Resistor [tolerance=±5% resistance=1k package=THT]
  U1 = Mini-360 DC-DC Buck converter [package=THT]
  C2 = Ceramic Capacitor [capacitance=100nF package="100 mil [THT, multilayer]"]
  C3 = Ceramic Capacitor [capacitance=100nF package="100 mil [THT, multilayer]"]
  C4 = Capacitor Polarized [package=cpol-radial-100uf-25v]
  microSD1 = MicroSD Card Module
  Часть2 = Arduino Pro Mini (3.3V)

nets:
  N1: OLED_I2C1.SDA, Часть2.A4
  N2: OLED_I2C1.SCK, Часть2.A5
  VCC: OLED_I2C1.VDD, U1.OUT+, C4.+, microSD1.VCC, Часть2.VCC
  GND: OLED_I2C1.GND, R1.Pin_0, X4.GND, R5.Pin_1, U1.IN-, U1.OUT-, C2.0, C3.0, C4.-, microSD1.GND, Часть2.GND
  N3: R2.Pin_0, R1.Pin_1, X3.VBUS
  N4: R2.Pin_1, C2.1, Часть2.A0
  N5: X3.GND, X4.VBUS, R3.Pin_0, U1.IN+
  N6: R3.Pin_1, R4.Pin_0, R5.Pin_0
  N7: R4.Pin_1, C3.1, Часть2.A1
  N8: microSD1.MISO, Часть2.MISO
  N9: microSD1.MOSI, Часть2.MOSI
  N10: microSD1.SCK, Часть2.SCK
  N11: microSD1.CS, Часть2.D4

custom parts:
  Mini-360 DC-DC Buck converter: Mini-360 DC-DC Buck converter. Tiny buck step down voltage converter, input voltage 4.75 to 23V output 1 to 17V adjustable. Available from ebay and the like.
