# Fritzing sketch USB-tester (saved by Fritzing 0.9.3b)

parts:
  OLED_I2C1 = OLED 128x64 I2C Monochrome Display
  R2 = Resistor [tolerance=±5% resistance=1k package=THT]
  R1 = Resistor [tolerance=±5% resistance=0.1 power=2W package=THT]
  USB_out = USB Connectors [package=usb-a-h]
  USB_in = USB Connectors [package=usb-a-h]
  R3 = Resistor [tolerance=±5% resistance=20k package=THT]
  R4 = Resistor [tolerance=±5% resistance=1k package=THT]
  R5 = Resistor [tolerance=±5% resistance=1k package=THT]
  U1 = Mini-360 DC-DC Buck converter [package=THT]
  C2 = Ceramic Capacitor [capacitance=100nF package="100 mil [THT, multilayer]"]
  C3 = Ceramic Capacitor [capacitance=100nF package="100 mil [THT, multilayer]"]
  C4 = Capacitor Polarized [package=cpol-radial-100uf-25v]
  microSD1 = MicroSD Card Module
  Часть3 = Arduino Nano (Rev3.0)

nets:
  N1: OLED_I2C1.SDA, Часть3.A4
  N2: OLED_I2C1.SCK, Часть3.A5
  VDD: OLED_I2C1.VDD, Часть3.3V3
  GND: OLED_I2C1.GND, R1.Pin_0, USB_in.GND, R5.Pin_1, U1.IN-, U1.OUT-, C2.0, C3.0, C4.-, microSD1.GND, Часть3.GND
  N3: R2.Pin_0, R1.Pin_1, USB_out.VBUS
  N4: R2.Pin_1, C2.1, Часть3.A0
  N5: USB_out.D-, USB_in.D+
  N6: USB_out.D+, USB_in.D-
  N7: USB_out.GND, USB_in.VBUS, R3.Pin_0, U1.IN+
  N8: R3.Pin_1, R4.Pin_0, R5.Pin_0
  N9: R4.Pin_1, C3.1, Часть3.A1
  VCC: U1.OUT+, C4.+, microSD1.VCC, Часть3.5V
  N10: microSD1.MISO, Часть3.D12/MISO
  N11: microSD1.MOSI, Часть3.D11/MOSI
  N12: microSD1.SCK, Часть3.D13/SCK
  N13: microSD1.CS, Часть3.D4

custom parts:
  Mini-360 DC-DC Buck converter: Mini-360 DC-DC Buck converter. Tiny buck step down voltage converter, input voltage 4.75 to 23V output 1 to 17V adjustable. Available from ebay and the like.
